# Fritzing sketch RGBPotenTouchFinal (saved by Fritzing 0.9.3b)
breadboards: 2

parts:
  Part1 = Arduino Uno (Rev3)
  R1 = Rotary Potentiometer (Small) [maximum_resistance=100kΩ package=THT]
  R2 = Rotary Potentiometer (Small) [maximum_resistance=100kΩ package=THT]
  R3 = Rotary Potentiometer (Small) [maximum_resistance=100kΩ package=THT]
  NEOPIXEL1 = Neopixel Strip -- White (60/m) [part_number=1138]
  NEOPIXEL2 = Neopixel Strip -- White (60/m) [part_number=1138]
  NEOPIXEL4 = Neopixel Strip -- White (60/m) [part_number=1138]
  Part3 = Adafruit MPR121

nets:
  N1: Part1.A0, R3.wiper
  N2: Part1.A1, R2.wiper
  N3: Part1.A2, R1.wiper
  N4: Part1.A4/SDA, Part3.SDA
  N5: Part1.A5/SCL, Part3.SCL
  N6: Part1.D8, NEOPIXEL4.DI
  N7: Part1.D6_PWM, NEOPIXEL1.DI
  N8: Part1.D7, NEOPIXEL2.DI
  +5V: Part1.5V, R1.leg2, R2.leg2, R3.leg2, NEOPIXEL1.+5V, NEOPIXEL2.+5V, NEOPIXEL4.+5V, Part3.VIN
  GND: Part1.GND, R1.leg1, R2.leg1, R3.leg1, NEOPIXEL1.GND, NEOPIXEL2.GND, NEOPIXEL4.GND, Part3.GND

custom parts:
  Neopixel Strip -- White (60/m): Neopixel Strip, White, 60 pixels per meter.
  Adafruit MPR121: Add lots of touch sensors to your next microcontroller project with this easy-to-use 12-channel capacitive touch sensor breakout board, starring the MPR121. This chip can handle up to 12 individual touch pads. The MPR121 has support for only I2C, which can be implemented with nearly any microcontroller. You can select one of 4 addresses with the ADDR pin, for a total of 48 capacitive touch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
